# Fritzing sketch HappyBirthday (saved by Fritzing 0.6.3b)
breadboards: 1

parts:
  Arduino1 = Arduino
  S1 = Pushbutton [package="[THT]"]
  R1 = Resistor [tolerance=±5% resistance=1k package=THT]
  J1 = Piezo Speaker
  LED1 = LED - 5mm [color="Green (555nm)" package="5 mm [THT]"]
  LED2 = LED - 5mm [color="Red (633nm)" package="5 mm [THT]"]
  LED3 = LED - 5mm [color="Red (633nm)" package="5 mm [THT]"]
  LED4 = LED - 5mm [color="Red (633nm)" package="5 mm [THT]"]
  LED5 = LED - 5mm [color="Yellow (585nm)" package="5 mm [THT]"]
  R2 = Resistor [tolerance=±5% resistance=220 package=THT]
  R3 = Resistor [tolerance=±5% resistance=220 package=THT]
  R4 = Resistor [tolerance=±5% resistance=220 package=THT]
  R5 = Resistor [tolerance=±5% resistance=220 package=THT]
  R6 = Resistor [tolerance=±5% resistance=220 package=THT]

nets:
  N1: Arduino1.D12, R6.Pin_1
  N2: Arduino1.D10, R2.Pin_0
  N3: Arduino1.D9, J1.pin2
  N4: Arduino1.D8, R3.Pin_1
  N5: Arduino1.D7, S1.Pin_3, S1.Pin_4, R1.Pin_0
  N6: Arduino1.D5, R5.Pin_1
  N7: Arduino1.D3, R4.Pin_0
  N8: Arduino1.+5V, S1.Pin_1, S1.Pin_2
  N9: Arduino1.GND, R1.Pin_1, J1.pin1, LED1.cathode, LED2.cathode, LED3.cathode, LED4.cathode, LED5.cathode
  N10: LED1.anode, R4.Pin_1
  N11: LED2.anode, R5.Pin_0
  N12: LED3.anode, R6.Pin_0
  N13: LED4.anode, R2.Pin_1
  N14: LED5.anode, R3.Pin_0
